# Fritzing sketch Untitled Sketch (saved by Fritzing 0.9.3b)

parts:
  元件1 = Arduino Uno (Rev3)
  LED1 = LED - 5mm [color="Red (633nm)" package="5 mm [THT]"]
  LED2 = LED - 5mm [color="Red (633nm)" package="5 mm [THT]"]
  LED3 = LED - 5mm [color="Red (633nm)" package="5 mm [THT]"]
  LED4 = LED - 5mm [color="Red (633nm)" package="5 mm [THT]"]

nets:
  N1: 元件1.GND, LED1.cathode, LED2.cathode, LED3.cathode, LED4.cathode
  N2: 元件1.D2, LED4.anode
  N3: 元件1.D3_PWM, LED3.anode
  N4: 元件1.D4, LED2.anode
  N5: 元件1.D5_PWM, LED1.anode

// code stored in the sketch: Untitled.ino
void setup() {
  pinMode(2, OUTPUT);
  pinMode(3, OUTPUT);
  pinMode(4, OUTPUT);
  pinMode(5, OUTPUT);

}

void loop() {
  digitalWrite(2,LOW);
  delay(500);
  digitalWrite(2,HIGH:;
  delay(500);
    digitalWrite(3,LOW);
  delay(500);
  digitalWrite(3,HIGH:;
  delay(500);
    digitalWrite(4,LOW);
  delay(500);
  digitalWrite(4,HIGH:;
  delay(500);
    digitalWrite(5,LOW);
  delay(500);
  digitalWrite(5,HIGH:;
  delay(500);
  

}
